# Fritzing sketch Tripwire (saved by Fritzing 0.9.3b)
breadboards: 1

parts:
  KY-008_Laserdiode1 = Laser [part_number=1219301 package=keys]
  Bauteil1 = Arduino Uno (Rev3)
  R1 = PHOTOCELL [package=photocell-kit]
  R2 = Resistor [tolerance=±5% resistance=220 package="0402 [SMD]"]

nets:
  N1: KY-008_Laserdiode1.connector0pin, Bauteil1.D3_PWM
  N2: KY-008_Laserdiode1.connector1pin, Bauteil1.5V, R1.P$1
  N3: KY-008_Laserdiode1.connector2pin, Bauteil1.GND, R2.Pin_1
  N4: Bauteil1.A0, R1.P$2, R2.Pin_0

custom parts:
  Laser: KEYES KY-008 650nm Laser Transmitter Module
