# Fritzing sketch Led Games (saved by Fritzing 0.9.3b)
breadboards: 1

parts:
  Part1 = Arduino Uno (Rev3)
  R1 = Resistor [tolerance=±5% resistance=220 package=THT]
  LED1 = LED - 5mm [color="Red (633nm)" package="5 mm [THT]"]
  R3 = Resistor [tolerance=±5% resistance=220 package=THT]
  LED3 = LED - 5mm [color="Red (633nm)" package="5 mm [THT]"]
  LED2 = LED - 5mm [color="Blue (430nm)" package="5 mm [THT]"]
  R2 = Resistor [tolerance=±5% resistance=220 package=THT]

nets:
  N1: Part1.D9_PWM, LED3.anode
  N2: Part1.D10_PWM/SS, LED2.anode
  N3: Part1.D11_PWM/MOSI, LED1.anode
  N4: Part1.GND, R1.Pin_1, R3.Pin_1, R2.Pin_1
  N5: R1.Pin_0, LED1.cathode
  N6: R3.Pin_0, LED3.cathode
  N7: LED2.cathode, R2.Pin_0
