# Fritzing sketch Smart House (saved by Fritzing 0.9.3b)
breadboards: 1

parts:
  Part1 = Arduino Uno (Rev3)
  R1 = Resistor [tolerance=±5% resistance=220 package=THT]
  LED1 = LED - 5mm [color="Red (633nm)" package="5 mm [THT]"]
  R2 = Resistor [tolerance=±5% resistance=220 package=THT]
  S1 = Pushbutton [package="[THT]"]
  R4 = PHOTOCELL [package=photocell-kit]
  R5 = Resistor [tolerance=±5% resistance=220 package=THT]
  LED2 = smd LED [color="Green (555nm)" package="0603 [SMD]"]
  R6 = Resistor [tolerance=±5% resistance=220 package=THT]
  S2 = Pushbutton [package="[THT]"]
  J1 = Piezo Speaker
  R7 = Rotary Potentiometer (Small) [maximum_resistance=100kΩ package=THT]
  LED4 = LED - 5mm [color="Blue (430nm)" package="5 mm [THT]"]
  R8 = Resistor [tolerance=±5% resistance=220 package=THT]
  LED3 = smd LED [color="White (8000K)" package="0603 [SMD]"]

nets:
  N1: Part1.A0, S1.Pin_3, S1.Pin_4
  N2: Part1.A1, R4.P$2, R5.Pin_0
  N3: Part1.A2, S2.Pin_3, S2.Pin_4
  N4: Part1.A3, R7.wiper
  N5: Part1.D9_PWM, LED4.anode
  N6: Part1.D10_PWM/SS, J1.pin2
  N7: Part1.D11_PWM/MOSI, LED3.anode
  N8: Part1.D12/MISO, LED2.anode
  N9: Part1.D13/SCK, LED1.anode
  N10: Part1.5V, S1.Pin_1, S1.Pin_2, R4.P$1, R7.leg1
  N11: Part1.GND, R1.Pin_1, R2.Pin_1, R5.Pin_1, R6.Pin_1, S2.Pin_1, S2.Pin_2, J1.pin1, R7.leg2, R8.Pin_1
  N12: R1.Pin_0, LED1.cathode
  N13: R2.Pin_0, LED2.cathode
  N14: R6.Pin_0, LED3.cathode
  N15: LED4.cathode, R8.Pin_0
