# Fritzing sketch Traffic Lights (saved by Fritzing 0.9.3b)
breadboards: 1

parts:
  Part1 = Arduino Uno (Rev3)
  R1 = Resistor [tolerance=±5% resistance=220 package=THT]
  LED1 = LED - 5mm [color="Green (570nm)" package="5 mm [THT]"]
  R3 = Resistor [tolerance=±5% resistance=220 package=THT]
  LED3 = LED - 5mm [color="Red (633nm)" package="5 mm [THT]"]  # not connected
  LED2 = LED - 5mm [color="Yellow (595nm)" package="5 mm [THT]"]
  R2 = Resistor [tolerance=±5% resistance=220 package=THT]
  S1 = Pushbutton [package="[THT]"]
  R4 = PHOTOCELL [package=photocell-kit]
  R5 = Resistor [tolerance=±5% resistance=220 package=THT]
  J1 = Piezo Speaker
  HC-SR04_Sensor_1 = HC-SR04 Ultrasonic Distance Sensor
  IR1 = TSOP312.., 314.. [package=THT]

nets:
  N1: Part1.A0, S1.Pin_3, S1.Pin_4
  N2: Part1.A1, R4.P$2, R5.Pin_0
  N3: Part1.D10_PWM/SS, LED2.anode
  N4: Part1.D11_PWM/MOSI, LED1.anode
  N5: Part1.D3_PWM, HC-SR04_Sensor_1.ECHO
  N6: Part1.D5_PWM, HC-SR04_Sensor_1.TRIG
  N7: Part1.D6_PWM, J1.pin2
  N8: Part1.D7, IR1.Data
  5V: Part1.5V, S1.Pin_1, S1.Pin_2, R4.P$1, HC-SR04_Sensor_1.VCC, IR1.Vs
  GND: Part1.GND, R1.Pin_1, R3.Pin_1, R2.Pin_1, R5.Pin_1, J1.pin1, HC-SR04_Sensor_1.GND, IR1.GND
  N9: R1.Pin_0, LED1.cathode
  N10: LED2.cathode, R2.Pin_0
