# Fritzing sketch _7 Segment Display - Copy (saved by Fritzing 0.9.3b)
breadboards: 1

parts:
  Part1 = Arduino Uno (Rev3) - ICSP
  R2 = Resistor [tolerance=±5% resistance=1k package="0402 [SMD]"]
  R1 = Resistor [tolerance=±5% resistance=1k package="0402 [SMD]"]
  DI1 = 7-Segment LED Display [package=THT]

nets:
  N1: Part1.D8, DI1.cathodeG
  N2: Part1.D9_PWM, DI1.cathodeDP
  N3: Part1.GND, R2.Pin_0, R1.Pin_1
  N4: Part1.D2, DI1.cathodeC
  N5: Part1.D3_PWM, DI1.cathodeD
  N6: Part1.D4, DI1.cathodeE
  N7: Part1.D5_PWM, DI1.cathodeB
  N8: Part1.D6_PWM, DI1.cathodeA
  N9: Part1.D7, DI1.cathodeF
  N10: R2.Pin_1, DI1.commAnode#7
  N11: R1.Pin_0, DI1.commAnode#2
