# Fritzing sketch _7 Segment Display (saved by Fritzing 0.9.3b)
breadboards: 1

parts:
  R1 = Resistor [tolerance=±5% resistance=1k package="0402 [SMD]"]
  Part1 = Arduino Uno (Rev3) - ICSP
  DI1 = 7-Segment LED Display [package=THT]
  R2 = Resistor [tolerance=±5% resistance=1k package="0402 [SMD]"]

nets:
  N1: R1.Pin_0, DI1.commAnode#2
  N2: R1.Pin_1, Part1.GND, R2.Pin_0
  N3: Part1.D8, DI1.cathodeG
  N4: Part1.D9_PWM, DI1.cathodeDP
  N5: Part1.D2, DI1.cathodeC
  N6: Part1.D3_PWM, DI1.cathodeD
  N7: Part1.D4, DI1.cathodeE
  N8: Part1.D5_PWM, DI1.cathodeB
  N9: Part1.D6_PWM, DI1.cathodeA
  N10: Part1.D7, DI1.cathodeF
  N11: DI1.commAnode#7, R2.Pin_1
