# Fritzing sketch joystick with leds (saved by Fritzing 0.9.3b)
breadboards: 1

parts:
  Part1 = Thumb Joystick
  Part2 = Arduino Uno (Rev3)
  LED4 = LED - 3mm [color="Red (633nm)" package="3 mm [THT]"]
  LED3 = LED - 3mm [color="Red (633nm)" package="3 mm [THT]"]
  LED2 = LED - 3mm [color="Red (633nm)" package="3 mm [THT]"]
  LED1 = LED - 3mm [color="Red (633nm)" package="3 mm [THT]"]
  R2 = Resistor [tolerance=±5% resistance=220 package="0805 [SMD]"]
  R1 = Resistor [tolerance=±5% resistance=220 package=THT]
  R4 = Resistor [tolerance=±5% resistance=220 package="0805 [SMD]"]
  R3 = Resistor [tolerance=±5% resistance=220 package="0805 [SMD]"]

nets:
  GND: Part1.GND, Part2.GND, R2.Pin_0, R1.Pin_1, R4.Pin_0, R3.Pin_0
  N1: Part1.SEL, Part2.D2
  N2: Part1.HORZ, Part2.A0
  N3: Part1.VERT, Part2.A1
  VCC: Part1.VCC, Part2.5V
  N4: Part2.D9_PWM, LED3.anode
  N5: Part2.D3_PWM, LED1.anode
  N6: Part2.D5_PWM, LED2.anode
  N7: Part2.D6_PWM, LED4.anode
  N8: LED4.cathode, R4.Pin_1
  N9: LED3.cathode, R3.Pin_1
  N10: LED2.cathode, R2.Pin_1
  N11: LED1.cathode, R1.Pin_0
