# Fritzing sketch lcd pot (saved by Fritzing 0.9.3b)
breadboards: 1

parts:
  Part1 = DeuLigne 1.1 - The Snootlab's LCD shield for Arduino
  Part2 = Arduino Uno (Rev3) - ICSP  # not connected
  U1 = POT [package=pot_alpha_rv16af-20]

nets:
  N1: Part1.A0, U1.S
  N2: Part1.+5V, U1.A
  N3: Part1.GND, U1.E
