# Fritzing sketch vu meter (saved by Fritzing 0.9.3b)
breadboards: 1

parts:
  Componente1 = Arduino Uno (Rev3)
  R1 = Resistor [tolerance=±5% resistance=330 package=THT]
  R2 = Resistor [tolerance=±5% resistance=330 package=THT]
  R3 = Resistor [tolerance=±5% resistance=330 package=THT]
  R4 = Resistor [tolerance=±5% resistance=330 package=THT]
  R5 = Resistor [tolerance=±5% resistance=330 package=THT]
  R6 = Resistor [tolerance=±5% resistance=330 package=THT]
  R7 = Resistor [tolerance=±5% resistance=330 package=THT]
  LED2 = LED - 5mm [color="Red (633nm)" package="5 mm [THT]"]
  LED3 = LED - 5mm [color="Red (633nm)" package="5 mm [THT]"]
  LED4 = LED - 5mm [color="Red (633nm)" package="5 mm [THT]"]
  LED5 = LED - 5mm [color="Red (633nm)" package="5 mm [THT]"]
  LED6 = LED - 5mm [color="Red (633nm)" package="5 mm [THT]"]
  LED7 = LED - 5mm [color="Red (633nm)" package="5 mm [THT]"]
  LED8 = LED - 5mm [color="Red (633nm)" package="5 mm [THT]"]
  FC-1 = Sound Sensor

nets:
  N1: Componente1.A0, FC-1.OUT
  N2: Componente1.D8, LED3.anode
  N3: Componente1.D9_PWM, LED2.anode
  N4: Componente1.D3_PWM, LED8.anode
  N5: Componente1.D4, LED7.anode
  N6: Componente1.D5_PWM, LED6.anode
  N7: Componente1.D6_PWM, LED5.anode
  N8: Componente1.D7, LED4.anode
  5V: Componente1.5V, FC-1.VCC
  GND: Componente1.GND, R1.Pin_0, R2.Pin_0, R3.Pin_0, R4.Pin_0, R5.Pin_0, R6.Pin_0, R7.Pin_0, FC-1.GND
  N9: R1.Pin_1, LED8.cathode
  N10: R2.Pin_1, LED7.cathode
  N11: R3.Pin_1, LED6.cathode
  N12: R4.Pin_1, LED2.cathode
  N13: R5.Pin_1, LED3.cathode
  N14: R6.Pin_1, LED4.cathode
  N15: R7.Pin_1, LED5.cathode

// code stored in the sketch: led vu meter with microphone and arduino.ino
/*
 * idea scopiazzata allegramente da:
 * https://sites.google.com/site/summerfuelrobots/arduino-sensor-tutorials/arduino-sound-sensor
This is the code to make a LED blink with sound.
You have to set the threshold so it' sensible enough to make the led blink.
 
You connect an LED to PIN13 and the Sound Sensor to Analog Pin 0
 */
 
int led5 = 3;
int led6 = 4;
int led7 = 5;
int led8 = 6;
int led9 = 7;
int led10 = 8;
int led11 = 9;


int volume;
int soglia = 25;
int incremento = 5;
 
void setup() {                
  //Serial.begin(9600); // For debugging

  pinMode(led5, OUTPUT);
  pinMode(led6, OUTPUT);
  pinMode(led7, OUTPUT);
  pinMode(led8, OUTPUT);
  pinMode(led9, OUTPUT);
  pinMode(led10, OUTPUT);
  pinMode(led11, OUTPUT);
 
}
 
void loop() {
  
  volume = analogRead(A0); // Reads the value from the Analog PIN A0
  /*
    //Debug mode
    Serial.println(volume);
    delay(100);
  */

  if(volume>=soglia){
    digitalWrite(led5, HIGH); //Turn ON Led
  }  
  else{
    digitalWrite(led5, LOW); // Turn OFF Led
  }
  if(volume>=soglia + incremento){
    digitalWrite(led6, HIGH); //Turn ON Led
  }  
  else{
    digitalWrite(led6, LOW); // Turn OFF Led
  }
  if(volume>=soglia + (incremento * 2)){
    digitalWrite(led7, HIGH); //Turn ON Led
  }  
  else{
    digitalWrite(led7, LOW); // Turn OFF Led
  }
  if(volume>=soglia + (incremento * 3)){
    digitalWrite(led8, HIGH); //Turn ON Led
  }  
  else{
    digitalWrite(led8, LOW); // Turn OFF Led
  }
  if(volume>=soglia + (incremento * 4)){
    digitalWrite(led9, HIGH); //Turn ON Led
  }  
  else{
    digitalWrite(led9, LOW); // Turn OFF Led
  }
  if(volume>=soglia + (incremento * 5)){
    digitalWrite(led10, HIGH); //Turn ON Led
  }  
  else{
    digitalWrite(led10, LOW); // Turn OFF Led
  }
  if(volume>=soglia + (incremento * 6)){
    digitalWrite(led11, HIGH); //Turn ON Led
  }  
  else{
    digitalWrite(led11, LOW); // Turn OFF Led
  }

 
 
}
